# Fritzing sketch Glade Schematic (saved by Fritzing 0.9.8b)

parts:
  Raspberry_Pi_1 = Raspberry Pi 3 [part_number=RPI-3-V1.2]
  Part1 = Jtron 1 Channel Optoisolated Relay Module [part_number="Power Relay 0" package=relay]
  Part2 = Jtron 1 Channel Optoisolated Relay Module [part_number="Trigger Relay 0" package=relay]
  Part3 = Jtron 1 Channel Optoisolated Relay Module [part_number="Power Relay 1" package=relay]
  Part4 = Jtron 1 Channel Optoisolated Relay Module [part_number="Trigger Relay 1" package=relay]
  Part5 = Jtron 1 Channel Optoisolated Relay Module [part_number="Power Relay 2" package=relay]
  Part6 = Jtron 1 Channel Optoisolated Relay Module [part_number="Trigger Relay 2" package=relay]
  S1 = SWITCH-MOMENTARY-2 [part_number="Relay Button 0" package=tactile-pth-12mm]
  S2 = SWITCH-MOMENTARY-2 [part_number="Relay Button 1" package=tactile-pth-12mm]
  S3 = SWITCH-MOMENTARY-2 [part_number="Relay Button 2" package=tactile-pth-12mm]
  LED1 = smd LED [color="Red (633nm)" package="0603 [SMD]"]
  LED2 = smd LED [color="Yellow (595nm)" package="0603 [SMD]"]
  S4 = SWITCH-MOMENTARY-2 [part_number="Start Operations Button" package=tactile-pth-12mm]
  R1 = Resistor [tolerance=±5% resistance=220 package="1206 [SMD]"]
  R2 = Resistor [tolerance=±5% resistance=220 package="1206 [SMD]"]
  R3 = Resistor [tolerance=±5% resistance=220 package="1206 [SMD]"]
  R4 = Resistor [tolerance=±5% resistance=220 package="1206 [SMD]"]
  R5 = Resistor [tolerance=±5% resistance=220 package="1206 [SMD]"]
  R6 = Resistor [tolerance=±5% resistance=220 package="1206 [SMD]"]
  VCC1 = Battery

nets:
  GND: Raspberry_Pi_1.GND, Part1.GND, Part2.GND, Part3.GND, Part4.GND, Part5.GND, Part6.GND, R1.Pin_1, R2.Pin_1, R3.Pin_1, R4.Pin_1, R5.Pin_1, R6.Pin_1, VCC1.-
  N1: Raspberry_Pi_1.GPIO17, Part1.IN1
  N2: Raspberry_Pi_1.GPIO27, LED1.anode
  N3: Raspberry_Pi_1.GPIO22, LED2.anode
  N4: Raspberry_Pi_1.3V3, S1.2, S2.2, S3.2, S4.2
  N5: Raspberry_Pi_1.GPIO6, S1.1, R3.Pin_0
  N6: Raspberry_Pi_1.GPIO13, S2.1, R4.Pin_0
  N7: Raspberry_Pi_1.GPIO19, S3.1, R5.Pin_0
  N8: Raspberry_Pi_1.GPIO26, S4.1, R6.Pin_0
  N9: Raspberry_Pi_1.GPIO16, Part6.IN1
  N10: Raspberry_Pi_1.GPIO12, Part2.IN1
  N11: Raspberry_Pi_1.GPIO24, Part5.IN1
  N12: Raspberry_Pi_1.GPIO23, Part3.IN1
  N13: Raspberry_Pi_1.GPIO18, Part4.IN1
  VCC: Part1.VCC, Part2.VCC, Part3.VCC, Part4.VCC, Part5.VCC, Part6.VCC, VCC1.+
  N14: LED1.cathode, R1.Pin_0
  N15: LED2.cathode, R2.Pin_0

notes:
  relay connections:
  NOs and commons
